// Logisim project Circuito 24hrs arrumar.circ as structural Verilog: 1 circuit, main circuit main
module main (
);

  wire and_1_out, and_2_out, and_3_out, and_4_out, and_5_out, clock_1_out, decodificador_1_p5,
       decodificador_1_p6, decodificador_1_p7, decodificador_1_p8, decodificador_1_p9, decodificador_1_p10,
       decodificador_1_p11, decodificador_2_p5, decodificador_2_p6, decodificador_2_p7, decodificador_2_p8,
       decodificador_2_p9, decodificador_2_p10, decodificador_2_p11, decodificador_3_p5, decodificador_3_p6,
       decodificador_3_p7, decodificador_3_p8, decodificador_3_p9, decodificador_3_p10, decodificador_3_p11,
       decodificador_4_p5, decodificador_4_p6, decodificador_4_p7, decodificador_4_p8, decodificador_4_p9,
       decodificador_4_p10, decodificador_4_p11, main_1_q0, main_1_q1, main_1_q2, main_1_q3, main_2_q0,
       main_2_q1, main_2_q2, main_2_q3, main_3_q0, main_3_q1, main_3_q2, main_3_q3, main_4_q0, main_4_q1,
       main_4_q2, main_4_q3;

  and and_1 (and_1_out, main_1_q0, main_1_q1);
  FlipFlopJK_zero_a_dez_main main_1 (
    .Clock(and_2_out), .Reset(and_1_out), .Q3(main_1_q3), .q2(main_1_q2), .q1(main_1_q1), .q0(main_1_q0));  // open: Set
  // Decodificador decodificador_1: pin names not known; wires that end beside it: main_1_q3, main_1_q2, main_1_q1, main_1_q0, decodificador_1_p5, decodificador_1_p6, decodificador_1_p7, decodificador_1_p8, decodificador_1_p9, decodificador_1_p10, decodificador_1_p11
  and and_2 (and_2_out, main_2_q2, main_2_q0);
  _7_Segment_Display u_7_segment_display_1 (
    .g(decodificador_1_p11), .f(decodificador_1_p10), .a(decodificador_1_p5), .b(decodificador_1_p6),
    .e(decodificador_1_p9), .d(decodificador_1_p8), .c(decodificador_1_p7));  // open: dp
  FlipFlopJK_zero_a_dez_main main_2 (
    .Clock(and_3_out), .Reset(and_2_out), .Q3(main_2_q3), .q2(main_2_q2), .q1(main_2_q1), .q0(main_2_q0));  // open: Set
  // Decodificador decodificador_2: pin names not known; wires that end beside it: main_2_q3, main_2_q2, main_2_q1, main_2_q0, decodificador_2_p5, decodificador_2_p6, decodificador_2_p7, decodificador_2_p8, decodificador_2_p9, decodificador_2_p10, decodificador_2_p11
  and and_3 (and_3_out, main_3_q2, main_3_q1);
  _7_Segment_Display u_7_segment_display_2 (
    .g(decodificador_2_p11), .f(decodificador_2_p10), .a(decodificador_2_p5), .b(decodificador_2_p6),
    .e(decodificador_2_p9), .d(decodificador_2_p8), .c(decodificador_2_p7));  // open: dp
  and and_4 (and_4_out, main_3_q1, main_3_q2);
  FlipFlopJK_zero_a_dez_main main_3 (
    .Clock(and_5_out), .Reset(and_4_out), .Q3(main_3_q3), .q2(main_3_q2), .q1(main_3_q1), .q0(main_3_q0));  // open: Set
  // Decodificador decodificador_3: pin names not known; wires that end beside it: main_3_q3, main_3_q2, main_3_q1, main_3_q0, decodificador_3_p5, decodificador_3_p6, decodificador_3_p7, decodificador_3_p8, decodificador_3_p9, decodificador_3_p10, decodificador_3_p11
  and and_5 (and_5_out, main_4_q3, main_4_q1);
  _7_Segment_Display u_7_segment_display_3 (
    .g(decodificador_3_p11), .f(decodificador_3_p10), .a(decodificador_3_p5), .b(decodificador_3_p6),
    .e(decodificador_3_p9), .d(decodificador_3_p8), .c(decodificador_3_p7));  // open: dp
  Clock clock_1 (.out(clock_1_out));
  FlipFlopJK_zero_a_dez_main main_4 (
    .Clock(clock_1_out), .Reset(and_5_out), .Q3(main_4_q3), .q2(main_4_q2), .q1(main_4_q1), .q0(main_4_q0));  // open: Set
  // Decodificador decodificador_4: pin names not known; wires that end beside it: main_4_q3, main_4_q2, main_4_q1, main_4_q0, decodificador_4_p5, decodificador_4_p6, decodificador_4_p7, decodificador_4_p8, decodificador_4_p9, decodificador_4_p10, decodificador_4_p11
  _7_Segment_Display u_7_segment_display_4 (
    .g(decodificador_4_p11), .f(decodificador_4_p10), .a(decodificador_4_p5), .b(decodificador_4_p6),
    .e(decodificador_4_p9), .d(decodificador_4_p8), .c(decodificador_4_p7));  // open: dp
endmodule
