// Logisim project Complemento de 2_4bits.circ as structural Verilog: 1 circuit, main circuit main
module main (
  input  A,
  input  B,
  input  C,
  input  D,
  output s1,
  output s2,
  output s3,
  output s4
);

  wire and_1_out, and_2_out, and_3_out, and_4_out, and_5_out, and_6_out, and_7_out, not_1_out, not_2_out,
       not_3_out, not_4_out, not_5_out, not_6_out, not_7_out, not_8_out, not_9_out, not_10_out, not_11_out;

  not not_1 (not_1_out, B);
  not not_2 (not_2_out, C);
  not not_3 (not_3_out, D);
  not not_4 (not_4_out, A);
  and and_1 (and_1_out, not_4_out, B);
  and and_2 (and_2_out, B, not_5_out, not_6_out);
  not not_5 (not_5_out, C);
  not not_6 (not_6_out, D);
  and and_3 (and_3_out, A, not_7_out, D);
  not not_7 (not_7_out, B);
  not not_8 (not_8_out, B);
  and and_4 (and_4_out, A, not_8_out, C);
  not not_9 (not_9_out, A);
  and and_5 (and_5_out, not_9_out, C);
  and and_6 (and_6_out, C, not_10_out);
  not not_10 (not_10_out, D);
  not not_11 (not_11_out, C);
  and and_7 (and_7_out, A, not_11_out, D);
  and and_8 (s1, A, not_1_out, not_2_out, not_3_out);
  or or_1 (s2, and_1_out, and_2_out, and_3_out, and_4_out);
  or or_2 (s3, and_5_out, and_6_out, and_7_out);

  assign s4 = D;
endmodule
