// Logisim project Demux 1;2.circ as structural Verilog: 1 circuit, main circuit main
module main (
  input  E0,
  input  ctrl,
  output S0,
  output S1
);

  wire not_1_out;

  not not_1 (not_1_out, ctrl);
  and and_1 (S0, E0, not_1_out);
  and and_2 (S1, E0, ctrl);
endmodule
