// Logisim project Demux 1;4.circ as structural Verilog: 1 circuit, main circuit main
module main (
  input  E0,
  input  ctrl0,
  input  ctrl1,
  output S0,
  output S1,
  output S2,
  output S3
);

  wire not_1_out, not_2_out;

  not not_1 (not_1_out, ctrl0);
  not not_2 (not_2_out, ctrl1);
  and and_1 (S0, not_1_out, not_2_out, E0);
  and and_2 (S1, not_1_out, ctrl1, E0);
  and and_3 (S2, ctrl0, not_2_out, E0);
  and and_4 (S3, ctrl0, ctrl1, E0);
endmodule
