// Logisim project FlipFlopJK_zero_a_dez.circ as structural Verilog: 1 circuit, main circuit main
module main (
  input  Clock,
  input  Set,
  input  Reset,
  output Q3,
  output q2,
  output q1,
  output q0
);

  wire j_k_ff_1_qn, j_k_ff_3_qn, or_1_out, or_2_out, q1_q0_out, q2_q1_q0_out;

  and q2_q1_q0 (q2_q1_q0_out, q2, q1_q0_out);
  and q1_q0 (q1_q0_out, q1, q0);
  J_K_Flip_Flop j_k_ff_1 (
    .J(q2_q1_q0_out), .clk(Clock), .K(q1), .Q(Q3), .Qn(j_k_ff_1_qn), .preset(Set), .reset(Reset));  // open: en
  J_K_Flip_Flop j_k_ff_2 (
    .J(q1_q0_out), .clk(Clock), .K(q1_q0_out), .Q(q2), .preset(Set), .reset(Reset));  // open: Qn, en
  or or_1 (or_1_out, Q3, q0);
  J_K_Flip_Flop j_k_ff_3 (
    .J(q0), .clk(Clock), .K(or_1_out), .Q(q1), .Qn(j_k_ff_3_qn), .preset(Set), .reset(Reset));  // open: en
  or or_2 (or_2_out, j_k_ff_3_qn, j_k_ff_1_qn);
  J_K_Flip_Flop j_k_ff_4 (.J(or_2_out), .clk(Clock), .K(1'b1), .Q(q0), .preset(Set), .reset(Reset));  // open: Qn, en
endmodule
