// Logisim project Mux 4;1.circ as structural Verilog: 1 circuit, main circuit main
module main (
  input  E0,
  input  E1,
  input  E2,
  input  E3,
  input  ctrl,
  input  ctrl_2,
  output S
);

  wire and_1_out, and_2_out, and_3_out, and_4_out, not_1_out, not_2_out;

  not not_1 (not_1_out, ctrl);
  not not_2 (not_2_out, ctrl_2);
  and and_1 (and_1_out, E0, not_2_out, not_1_out);
  and and_2 (and_2_out, E1, not_1_out, ctrl_2);
  and and_3 (and_3_out, E2, ctrl, not_2_out);
  and and_4 (and_4_out, E3, ctrl, ctrl_2);
  or or_1 (S, and_1_out, and_2_out, and_3_out, and_4_out);
endmodule
