// Logisim project Sequencia_3_1_0_2_Com_Flip_Flop_JK.circ as structural Verilog: 1 circuit, main circuit main
module main (
  input  in_1,
  output q1,
  output q0
);

  wire j_k_ff_1_qn, j_k_ff_2_qn;

  J_K_Flip_Flop j_k_ff_1 (.J(j_k_ff_2_qn), .clk(in_1), .K(q0), .Q(q1), .Qn(j_k_ff_1_qn));  // open: preset, en, reset
  J_K_Flip_Flop j_k_ff_2 (.J(q1), .clk(in_1), .K(j_k_ff_1_qn), .Q(q0), .Qn(j_k_ff_2_qn));  // open: preset, en, reset
endmodule
