// Logisim project Subtrador Completo 7 segmentos.circ as structural Verilog: 1 circuit, main circuit main
module main (
  input  A3,
  input  A2,
  input  A1,
  input  A0,
  input  B3,
  input  B2,
  input  B1,
  input  B0
);

  wire decodificador_1_p5, decodificador_1_p6, decodificador_1_p7, decodificador_1_p8, decodificador_1_p9,
       decodificador_1_p10, decodificador_1_p11, subtrador_1_s, subtrador_2_bout, subtrador_2_s,
       subtrador_3_bout, subtrador_3_s, subtrador_4_bout, subtrador_4_s;

  Subtrador subtrador_1 (.A(A3), .B(B3), .Cin(subtrador_2_bout), .S(subtrador_1_s));  // open: Bout
  Subtrador subtrador_2 (.A(A2), .B(B2), .Cin(subtrador_3_bout), .S(subtrador_2_s), .Bout(subtrador_2_bout));
  Subtrador subtrador_3 (.A(A1), .B(B1), .Cin(subtrador_4_bout), .S(subtrador_3_s), .Bout(subtrador_3_bout));
  Subtrador subtrador_4 (.A(A0), .B(B0), .Cin(1'b0), .S(subtrador_4_s), .Bout(subtrador_4_bout));
  // Decodificador decodificador_1: pin names not known; wires that end beside it: subtrador_1_s, subtrador_2_s, subtrador_3_s, subtrador_4_s, decodificador_1_p5, decodificador_1_p6, decodificador_1_p7, decodificador_1_p8, decodificador_1_p9, decodificador_1_p10, decodificador_1_p11
  _7_Segment_Display u_7_segment_display_1 (
    .g(decodificador_1_p11), .f(decodificador_1_p10), .a(decodificador_1_p5), .b(decodificador_1_p6),
    .e(decodificador_1_p9), .d(decodificador_1_p8), .c(decodificador_1_p7));  // open: dp
endmodule
