// Logisim project Teste circuito JK.circ as structural Verilog: 1 circuit, main circuit main
module main (
  output out_1,
  output out_2,
  output out_3,
  output out_4
);

  wire and_1_out, and_2_out;

  and and_1 (and_1_out, out_2, out_3, out_4);
  and and_2 (and_2_out, out_3, out_4);
  J_K_Flip_Flop j_k_ff_1 (.J(and_1_out), .K(out_3), .Q(out_1));  // open: clk, Qn, preset, en, reset
  J_K_Flip_Flop j_k_ff_2 (.J(and_2_out), .K(and_2_out), .Q(out_2));  // open: clk, Qn, preset, en, reset
  J_K_Flip_Flop j_k_ff_3 (.J(out_4), .Q(out_3));  // open: clk, K, Qn, preset, en, reset
  J_K_Flip_Flop j_k_ff_4 (.K(1'b1), .Q(out_4));  // open: J, clk, Qn, preset, en, reset
endmodule
